# Fritzing sketch Untitled Sketch 2 (saved by Fritzing 0.8.3b)
breadboards: 1

parts:
  Bauteil1 = Arduino Mega 2560 (Rev3)
  R1 = Resistor [tolerance=±5% resistance=220 package=THT]
  R2 = Resistor [tolerance=±5% resistance=220 package=THT]
  R3 = Resistor [tolerance=±5% resistance=220 package=THT]
  LED1 = LED - 5mm [color="Red (633nm)" package="5 mm [THT]"]
  LED2 = LED - 5mm [color="Yellow (595nm)" package="5 mm [THT]"]
  LED3 = LED - 5mm [color="Green (570nm)" package="5 mm [THT]"]
  LED4 = LED - 5mm [color="Red (633nm)" package="5 mm [THT]"]
  LED5 = LED - 5mm [color="Green (570nm)" package="5 mm [THT]"]
  R4 = Resistor [tolerance=±5% resistance=220 package=THT]
  R5 = Resistor [tolerance=±5% resistance=220 package=THT]
  S1 = Pushbutton [package="[THT]"]
  R6 = Resistor [tolerance=±5% resistance=10k package=THT]

nets:
  N1: Bauteil1.D12_PWM, S1.Pin_3, S1.Pin_4, R6.Pin_0
  N2: Bauteil1.D10_PWM, R1.Pin_0
  N3: Bauteil1.D8_PWM, R2.Pin_0
  N4: Bauteil1.5V, LED1.anode, LED2.anode, LED3.anode, LED4.anode, LED5.anode, S1.Pin_1, S1.Pin_2
  N5: Bauteil1.GND, R6.Pin_1
  N6: Bauteil1.D2_PWM, R4.Pin_0
  N7: Bauteil1.D4_PWM, R5.Pin_0
  N8: Bauteil1.D6_PWM, R3.Pin_0
  N9: R1.Pin_1, LED1.cathode
  N10: R2.Pin_1, LED2.cathode
  N11: R3.Pin_1, LED3.cathode
  N12: LED4.cathode, R5.Pin_1
  N13: LED5.cathode, R4.Pin_1
