# Fritzing sketch Untitled Sketch 2 (saved by Fritzing 0.8.3b)
breadboards: 2

parts:
  Bauteil1 = Arduino Mega 2560 (Rev3)
  LED1 = LED - 5mm [color="Red (633nm)" package="5 mm [THT]"]
  LED2 = LED - 5mm [color="Red (633nm)" package="5 mm [THT]"]
  LED3 = LED - 5mm [color="Red (633nm)" package="5 mm [THT]"]  # not connected
  LED4 = LED - 5mm [color="Red (633nm)" package="5 mm [THT]"]
  LED5 = LED - 5mm [color="Yellow (595nm)" package="5 mm [THT]"]
  LED6 = LED - 5mm [color="Yellow (595nm)" package="5 mm [THT]"]
  LED7 = LED - 5mm [color="Yellow (595nm)" package="5 mm [THT]"]
  LED8 = LED - 5mm [color="Yellow (595nm)" package="5 mm [THT]"]  # not connected
  LED9 = LED - 5mm [color="Green (570nm)" package="5 mm [THT]"]
  LED10 = LED - 5mm [color="Green (570nm)" package="5 mm [THT]"]  # not connected
  LED11 = LED - 5mm [color="Green (570nm)" package="5 mm [THT]"]
  LED12 = LED - 5mm [color="Green (570nm)" package="5 mm [THT]"]
  R1 = Resistor [tolerance=±5% resistance=330 package=THT]
  R2 = Resistor [tolerance=±5% resistance=330 package=THT]
  R3 = Resistor [tolerance=±5% resistance=330 package=THT]
  R4 = Resistor [tolerance=±5% resistance=330 package=THT]
  R5 = Resistor [tolerance=±5% resistance=330 package=THT]
  R6 = Resistor [tolerance=±5% resistance=330 package=THT]
  R7 = Resistor [tolerance=±5% resistance=330 package=THT]
  R8 = Resistor [tolerance=±5% resistance=330 package=THT]
  R9 = Resistor [tolerance=±5% resistance=330 package=THT]
  R10 = Resistor [tolerance=±5% resistance=330 package=THT]
  R11 = Resistor [tolerance=±5% resistance=330 package=THT]
  R12 = Resistor [tolerance=±5% resistance=330 package=THT]

nets:
  N1: Bauteil1.D12_PWM, R6.Pin_1
  N2: Bauteil1.D11_PWM, R5.Pin_1
  N3: Bauteil1.D10_PWM, R4.Pin_1
  N4: Bauteil1.D9_PWM, R10.Pin_0
  N5: Bauteil1.D8_PWM, R11.Pin_0
  N6: Bauteil1.GND, LED1.anode, LED2.anode, LED4.anode, LED5.anode, LED6.anode, LED7.anode, LED9.anode, LED11.anode, LED12.anode
  N7: Bauteil1.D1_TX0, R9.Pin_1
  N8: Bauteil1.D2_PWM, R8.Pin_1
  N9: Bauteil1.D3_PWM, R7.Pin_1
  N10: Bauteil1.D4_PWM, R1.Pin_0
  N11: Bauteil1.D5_PWM, R2.Pin_0
  N12: Bauteil1.D6_PWM, R3.Pin_0
  N13: Bauteil1.D7_PWM, R12.Pin_0
  N14: LED1.cathode, R1.Pin_1
  N15: LED2.cathode, R12.Pin_1
  N16: LED4.cathode, R4.Pin_0
  N17: LED5.cathode, R11.Pin_1
  N18: LED6.cathode, R5.Pin_0
  N19: LED7.cathode, R2.Pin_1
  N20: LED9.cathode, R10.Pin_1
  N21: LED11.cathode, R6.Pin_0
  N22: LED12.cathode, R3.Pin_1
