# Fritzing sketch Lauflicht (saved by Fritzing 0.8.3b)
breadboards: 1

parts:
  Bauteil1 = Arduino Mega 2560 (Rev3)
  LED1 = LED - 5mm [color="Green (555nm)" package="5 mm [THT]"]
  LED2 = LED - 5mm [color="Blue (525nm)" package="5 mm [THT]"]
  LED3 = LED - 5mm [color="Yellow (595nm)" package="5 mm [THT]"]
  LED4 = LED - 5mm [color="Red (660nm)" package="5 mm [THT]"]
  LED5 = LED - 5mm [color="White (4500K)" package="5 mm [THT]"]
  LED6 = LED - 5mm [color="Green (555nm)" package="5 mm [THT]"]
  LED7 = LED - 5mm [color="Blue (525nm)" package="5 mm [THT]"]
  LED8 = LED - 5mm [color="Yellow (595nm)" package="5 mm [THT]"]
  LED9 = LED - 5mm [color="Red (660nm)" package="5 mm [THT]"]
  LED10 = LED - 5mm [color="White (4500K)" package="5 mm [THT]"]
  R1 = Resistor [tolerance=±5% resistance=330 package=THT]
  R2 = Resistor [tolerance=±5% resistance=330 package=THT]
  R3 = Resistor [tolerance=±5% resistance=330 package=THT]
  R4 = Resistor [tolerance=±5% resistance=330 package=THT]
  R5 = Resistor [tolerance=±5% resistance=330 package=THT]
  R6 = Resistor [tolerance=±5% resistance=330 package=THT]
  R7 = Resistor [tolerance=±5% resistance=330 package=THT]
  R8 = Resistor [tolerance=±5% resistance=330 package=THT]
  R9 = Resistor [tolerance=±5% resistance=330 package=THT]
  R10 = Resistor [tolerance=±5% resistance=330 package=THT]
  S1 = Pushbutton [package="[THT]"]
  R11 = Resistor [tolerance=±5% resistance=10k package=THT]

nets:
  N1: Bauteil1.D13_PWM, R1.Pin_0
  N2: Bauteil1.D12_PWM, R2.Pin_0
  N3: Bauteil1.D11_PWM, R3.Pin_0
  N4: Bauteil1.D10_PWM, R4.Pin_0
  N5: Bauteil1.D9_PWM, R5.Pin_0
  N6: Bauteil1.D8_PWM, R6.Pin_0
  N7: Bauteil1.5V, S1.Pin_1, S1.Pin_2
  N8: Bauteil1.GND, LED1.anode, LED2.anode, LED3.anode, LED4.anode, LED5.anode, LED6.anode, LED7.anode, LED8.anode, LED9.anode, LED10.anode, R11.Pin_1
  N9: Bauteil1.D2_PWM, S1.Pin_3, S1.Pin_4, R11.Pin_0
  N10: Bauteil1.D4_PWM, R10.Pin_0
  N11: Bauteil1.D5_PWM, R9.Pin_0
  N12: Bauteil1.D6_PWM, R8.Pin_0
  N13: Bauteil1.D7_PWM, R7.Pin_0
  N14: LED1.cathode, R1.Pin_1
  N15: LED2.cathode, R2.Pin_1
  N16: LED3.cathode, R3.Pin_1
  N17: LED4.cathode, R4.Pin_1
  N18: LED5.cathode, R5.Pin_1
  N19: LED6.cathode, R6.Pin_1
  N20: LED7.cathode, R7.Pin_1
  N21: LED8.cathode, R8.Pin_1
  N22: LED9.cathode, R9.Pin_1
  N23: LED10.cathode, R10.Pin_1
